# Fritzing sketch 아두이노 회로도1 (saved by Fritzing 1.0.5)
breadboards: 1

parts:
  부품1 = Arduino Mega 2560 (Rev3)
  부품4 = Motor Driver 1A Dual TB6612FNG
  부품5 = Motor Driver 1A Dual TB6612FNG
  VCC1 = Battery block 9V [internal_resistance=0.1Ω]

nets:
  N1: 부품1.A9, 부품5.PWM1
  N2: 부품1.A10, 부품5.PWM2
  N3: 부품1.A11, 부품4.PWM1
  N4: 부품1.A12, 부품4.PWM2
  N5: 부품1.5V, 부품5.DIR2
  VCC: 부품1.D22, 부품1.D28, 부품4.VCC, 부품4.DIR1, 부품4.VM(<12v), 부품5.VCC, 부품5.DIR1, 부품5.VM(<12v), VCC1.+
  N6: 부품1.D29, 부품4.DIR2
  GND: 부품4.GND, 부품5.GND, VCC1.-

custom parts:
  Motor Driver 1A Dual TB6612FNG: The TB6612FNG motor driver can control up to two DC motors at a constant current of 1.2A (3.2A peak). Two input signals (IN1 and IN2) can be used to control the motor in one of four function modes - CW, CCW, short-brake, and stop. The two motor outputs (A and B) can be separately controlled, the speed of each motor is controlled via a PWM input signal with a frequency up to 100kHz. The STBY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
